# Fritzing sketch metronome (saved by Fritzing 0.7.11b)
breadboards: 1

parts:
  Arduino1 = Arduino
  S1 = Pushbutton [package="[THT]"]
  R1 = Resistor [tolerance=±5% resistance=10k package=THT]
  LED1 = LED - 5mm [color="Red (633nm)" package="5 mm [THT]"]
  R2 = Resistor [tolerance=±5% resistance=330 package=THT]
  J1 = Piezo Speaker

nets:
  N1: Arduino1.D6, LED1.anode
  N2: Arduino1.D5, J1.pin2
  N3: Arduino1.+5V, S1.Pin_3, S1.Pin_4
  N4: Arduino1.GND, R1.Pin_1, R2.Pin_0, J1.pin1
  N5: S1.Pin_1, S1.Pin_2, R1.Pin_0
  N6: LED1.cathode, R2.Pin_1
